# Fritzing sketch hardware_full_board(inc.OLED)_diagram (saved by Fritzing 1.0.4)
breadboards: 1

parts:
  Mod1 = Raspberry Pi Pico W
  LED1 = LED - 5mm [color="Red (633nm)" current=0.030A package="5 mm [THT]"]
  LED2 = LED - 5mm [color="Green (565nm)" current=0.030A package="5 mm [THT]"]
  U1 = POT [knob_status=50% power=0.5W package=alps_pot]
  OLED_I2C1 = OLED 128x64 I2C Monochrome Display
  R1 = Resistor [tolerance=±5% resistance=220 package="1206 [SMD]"]
  R2 = Resistor [tolerance=±5% resistance=220 package="1206 [SMD]"]
  R3 = Resistor [tolerance=±5% resistance=220 package="1206 [SMD]"]

nets:
  N1: Mod1.pin_1, R2.Pin_1
  N2: Mod1.pin_2, R1.Pin_1
  N3: Mod1.pin_3, Mod1.pin_8, Mod1.pin_13, Mod1.pin_18, Mod1.pin_23, Mod1.pin_28, Mod1.pin_33, Mod1.pin_38, Mod1.pin_42, LED1.cathode, LED2.cathode, U1.A, OLED_I2C1.GND
  N4: Mod1.pin_11, OLED_I2C1.SDA
  N5: Mod1.pin_12, OLED_I2C1.SCK
  N6: Mod1.pin_31, R3.Pin_1
  N7: Mod1.pin_36, U1.E, OLED_I2C1.VDD
  N8: LED1.anode, R1.Pin_0
  N9: LED2.anode, R2.Pin_0
  N10: U1.S, R3.Pin_0

notes:
  Това е схемата на завършената пълна платка за проекта VitalLink.
  е пълната версия(вкл. OLED).

custom parts:
  Raspberry Pi Pico W: Raspberry Pi Pico W. Based around the RP2040 microcontroller the Pico W is a low cost microcontroller device bringing Raspberry Pi quality, cost, and easy of use to the microcontroller space. The areas marked KEEPOUT in pcb silkscreen should not have traces running through them to avoid shorts on a soldered in module!
